# Fritzing sketch ATTiny85 (saved by Fritzing 0.9.3b)
circuit board: 1.65464cm x 5.34433cm
breadboards: 1

parts:
  U1 = attiny85 [package=dip]
  J2 = female pin header, 2 pins [form="♀ (female)"]
  J1 = male pin header, 4 pins [form="♂ (male)"]

nets:
  N1: U1.Pin_1, J1.pin1
  N2: U1.Pin_4, J2.pin1
  N3: U1.Pin_5, J1.pin2
  N4: U1.Pin_6, J1.pin3
  N5: U1.Pin_7, J1.pin4
  N6: U1.Pin_8, J2.pin2

notes:
  Anoop
