# Fritzing sketch PCBTMP36rpi5v3.3 (saved by Fritzing 0.9.3b)
circuit board: 2.56422cm x 5.00152cm
breadboards: 1

parts:
  U1 = attiny85 [package=dip]
  R1 = Resistor [tolerance=±5% resistance=4.7k package=THT]
  R2 = Resistor [tolerance=±5% resistance=4.7k package=THT]
  J10 = female pin header, 1 pin [form="♀ (female)"]
  J15 = female pin header, 2 pins [form="♀ (female)"]
  J16 = female pin header, 2 pins [form="♀ (female)"]
  J17 = female pin header, 1 pin [form="♀ (female)"]
  J19 = female pin header, 1 pin [form="♀ (female)"]  # not connected
  J20 = female pin header, 2 pins [form="♀ (female)"]
  J21 = female pin header, 1 pin [form="♀ (female)"]
  J22 = female pin header, 1 pin [form="♀ (female)"]
  J18 = female pin header, 1 pin [form="♀ (female)"]

nets:
  N1: U1.Pin_2, J10.pin1
  N2: U1.Pin_4, J15.pin2, J17.pin1, J20.pin1
  N3: U1.Pin_5, R1.Pin_0, J16.pin1
  N4: U1.Pin_7, R2.Pin_0, J16.pin2
  N5: U1.Pin_8, R1.Pin_1, R2.Pin_1, J21.pin1
  N6: J22.pin1, J18.pin1

notes:
  Anoopjot
