# Fritzing sketch PCBwithTMP36Arduino (saved by Fritzing 0.9.3b)
circuit board: 2.60415cm x 5.22702cm
breadboards: 1

parts:
  U1 = attiny85 [package=dip]
  R1 = Resistor [tolerance=±5% resistance=4.7k package=THT]
  R2 = Resistor [tolerance=±5% resistance=4.7k package=THT]
  J3 = female pin header, 2 pins [form="♀ (female)"]
  J4 = female pin header, 2 pins [form="♀ (female)"]
  J10 = female pin header, 1 pin [form="♀ (female)"]
  J11 = female pin header, 1 pin [form="♀ (female)"]
  J12 = female pin header, 1 pin [form="♀ (female)"]

nets:
  N1: U1.Pin_2, U1.Pin_4, J4.pin2, J10.pin1, J12.pin1
  N2: U1.Pin_5, R1.Pin_0, J3.pin1
  N3: U1.Pin_7, R2.Pin_0, J3.pin2
  N4: U1.Pin_8, R1.Pin_1, R2.Pin_1, J4.pin1, J11.pin1

notes:
  Anoop
